# Fritzing sketch HR board (saved by Fritzing 0.7.1b)
perfboards: 2

parts:
  Arduino1 = Arduino
  R1 = Resistor [tolerance=±5% resistance=33k package=THT]
  J1 = female pin header, 4 pins [form="♀ (female)"]  # not connected
  J2 = female pin header, 4 pins [form="♀ (female)"]  # not connected
  J3 = female pin header, 4 pins [form="♀ (female)"]  # not connected
  U1 = attiny85 [package=dip]  # not connected
  J4 = male pin header, 8 pins [form="♂ (male)"]  # not connected
  J5 = male pin header, 8 pins [form="♂ (male)"]  # not connected
  XTAL1 = CRYSTAL - kHz [frequency="32 kHz"]  # not connected
  R2 = Resistor [tolerance=±5% resistance=33k package=THT]

nets:
  N1: Arduino1.+5V, R1.Pin_0, R2.Pin_0
  N2: Arduino1.A4, R1.Pin_1
  N3: Arduino1.A5, R2.Pin_1

notes:
  polar
